# Fritzing sketch 7-Segment Extendable Display (saved by Fritzing 0.9.3b)
circuit board: 2.12171cm x 6.51974cm
breadboards: 1

parts:
  J1 = shrouded pin header, 6 pins [form="♂ (shrouded male)"]
  7_Segment1 = 7 Segment Display
  R1 = Resistor [tolerance=±5% resistance=220 package=THT]
  J2 = female pin header, 2 pins [form="♀ (female)"]
  U1 = atmega168 [package=dip]
  J3 = female pin header, 6 pins [form="♀ (female)"]
  J4 = female pin header, 6 pins [form="♀ (female)"]

nets:
  N1: J1.pin1, R1.Pin_1, J2.pin2, U1.GND#7, J3.pin1, J4.pin1
  N2: J1.pin2, J1.pin3, U1.A5, J3.pin3, J3.pin5, J4.pin3, J4.pin5
  N3: J1.pin4, J1.pin5, J1.pin6, U1.VCC, U1.A4, J3.pin2, J3.pin4, J3.pin6, J4.pin2, J4.pin4, J4.pin6
  N4: 7_Segment1.Segment_E, U1.D6_(PWM)
  N5: 7_Segment1.Segment_D, U1.D5_(PWM)
  N6: 7_Segment1.common_cathode, R1.Pin_0, J2.pin1
  N7: 7_Segment1.Segment_C, U1.D4
  N8: 7_Segment1.Segment_DP, U1.D9_(PWM)
  N9: 7_Segment1.Segment_B, U1.D3_(PWM)
  N10: 7_Segment1.Segment_A, U1.D2
  N11: 7_Segment1.Segment_F, U1.D7
  N12: 7_Segment1.Segment_G, U1.D8
