# Fritzing sketch 7805 Assembly (saved by Fritzing 0.9.3b)
circuit board: 1.90332cm x 7.19444cm
breadboards: 1

parts:
  C1 = Ceramic Capacitor [capacitance=10µF voltage=50V package="100 mil [THT, multilayer]"]
  C2 = Ceramic Capacitor [capacitance=10µF voltage=50V package="100 mil [THT, multilayer]"]
  LED1 = LED - 5mm [color="Red (633nm)" package="5 mm [THT]"]
  J1 = male pin header, 3 pins [form="♂ (male)"]
  U3 = Voltage Regulator - 5V [package="TO220 [THT]"]
  U4 = Voltage Regulator - 5V [package="TO220 [THT]"]
  U1 = Voltage Regulator - 5V [package="TO220 [THT]"]
  R1 = Resistor [tolerance=±5% resistance=220 package=THT]
  Pad1 = Pad [width=1.82311833650069 height=1.8982202698213462 connect=center]
  U2 = Voltage Regulator - 5V [package="TO220 [THT]"]
  J3 = Power plug
  J2 = screw terminal, 3 pins

nets:
  GND: C1.0, C2.0, J1.pin2, U3.GND, U4.GND, U1.GND, R1.Pin_0, Pad1.pad, U2.GND, J3.GND, J2.pin2
  N1: C1.1, J1.pin1, U3.input_voltage, U4.input_voltage, U1.input_voltage, U2.input_voltage, J3.VCC, J2.pin1
  N2: C2.1, LED1.anode, J1.pin3, U3.output_voltage, U4.output_voltage, U1.output_voltage, U2.output_voltage, J2.pin3
  N3: LED1.cathode, R1.Pin_1

notes:
  7805 Assembly V.0
