# Fritzing sketch RTC (saved by Fritzing 0.9.3b)
circuit board: 5.26106cm x 2.21583cm
breadboards: 1

parts:
  XTAL1 = Crystal [frequency="32 MHz" package=THT]
  BAT1 = Battery Holders [package=battcom_20mm_pth]
  IC1 = DS1307 [package=THT]
  CONN1 = male pin header, 8 pins [form="♂ (male)"]
  CONN = male pin header, 8 pins [form="♂ (male)"]
  C1 = Ceramic Capacitor [capacitance=10pF voltage=10V package="100 mil [THT, multilayer]"]
  C2 = Ceramic Capacitor [capacitance=10pF voltage=10V package="100 mil [THT, multilayer]"]

nets:
  N1: XTAL1.pin_0, IC1.X2_-_Crystal, C1.1
  N2: XTAL1.pin_1, IC1.X1_-_Crystal, C2.0
  N3: BAT1.+, IC1.Vbat_-_Backup_Supply
  N4: BAT1.-, IC1.0V, CONN1.pin1, CONN1.pin8, CONN.pin1, CONN.pin8, C1.0, C2.1
  N5: IC1.SDA_-_I2C_Data, CONN1.pin3, CONN1.pin6, CONN.pin3, CONN.pin6
  N6: IC1.SCL_-_I2C_Clock, CONN1.pin2, CONN1.pin7, CONN.pin2, CONN.pin7
  N7: IC1.+V, CONN1.pin4, CONN1.pin5, CONN.pin4, CONN.pin5

notes:
  0V SCL SDA 5V 5V SDA SCL 0V
  Circuit V.0
  Bottom Robot
  RTC Module V.0
