# Fritzing sketch RTC (saved by Fritzing 0.9.3b)
circuit board: 5.1824cm x 2.21583cm
breadboards: 1

parts:
  CONN = male pin header, 8 pins [form="♂ (male)"]
  IC1 = DS1307 [package=THT]
  BAT1 = Battery Holders [package=battcom_20mm_pth]
  XTAL1 = Crystal [frequency="32 MHz" package=THT]
  CONN1 = male pin header, 8 pins [form="♂ (male)"]

nets:
  N1: CONN.pin1, CONN.pin8, IC1.0V, BAT1.-, CONN1.pin1, CONN1.pin8
  N2: CONN.pin2, CONN.pin7, IC1.SCL_-_I2C_Clock, CONN1.pin2, CONN1.pin7
  N3: CONN.pin3, CONN.pin6, IC1.SDA_-_I2C_Data, CONN1.pin3, CONN1.pin6
  N4: CONN.pin4, CONN.pin5, IC1.+V, CONN1.pin4, CONN1.pin5
  N5: IC1.X1_-_Crystal, XTAL1.pin_1
  N6: IC1.X2_-_Crystal, XTAL1.pin_0
  N7: IC1.Vbat_-_Backup_Supply, BAT1.+

notes:
  0V SCL SDA 5V 5V SDA SCL 0V
  Circuit V.0
  Bottom Robot
  RTC Module V.0
